# Fritzing sketch Bicycle Smart Dashboard (saved by Fritzing 0.9.4)
breadboards: 1

parts:
  D_Flip_Flop = SN74LS14N [package="DIP14 [THT]"]
  Adafruit_Powerboost_500 = PowerBoost 500 Charger
  OLED_I2C1 = OLED 128x64 I2C Monochrome Display
  U1 = ESP32S-HiLetgo [part_number=ESP32S-HiLetgo]
  S1 = Reed switch [package=THT]
  U2 = LIPO-2000mAh [package=lipo-2000]
  R2 = PHOTOCELL [package=photocell]
  R3 = Resistor [tolerance=±5% resistance=10k package="0805 [SMD]"]
  R4 = Resistor [tolerance=±5% resistance=470 package="0805 [SMD]"]
  LED1 = smd LED [color="Red (633nm)" package="0805 [SMD]"]
  U3 = Voltage Regulator - 3.3V [package="TO220 [THT]"]
  S2 = Toggle Switch [package=THT]

nets:
  N1: D_Flip_Flop.1A, U1.GPIO25
  N2: D_Flip_Flop.1Y, U1.GPIO39
  N3: D_Flip_Flop.2A, U1.GPIO15, S1.pin_2
  N4: D_Flip_Flop.3A, U1.GPIO26
  GND: D_Flip_Flop.GND, Adafruit_Powerboost_500.GND, OLED_I2C1.GND, U1.GND, S1.pin_1, R3.Pin_0, LED1.cathode, U3.GND, S2.COM
  N5: D_Flip_Flop.VCC, Adafruit_Powerboost_500.5.0V, R2.P$2, U3.input_voltage
  N6: Adafruit_Powerboost_500.GND_BAT_IN, U2.-
  N7: Adafruit_Powerboost_500.VBAT_IN, U2.+
  N8: Adafruit_Powerboost_500.ENABLE, S2.L1
  N9: OLED_I2C1.SDA, U1.GPIO21
  N10: OLED_I2C1.SCK, U1.GPIO22
  N11: OLED_I2C1.VDD, U1.GPIO16
  N12: U1.3.3, U3.output_voltage
  N13: U1.GPIO32, R2.P$1, R3.Pin_1
  N14: U1.GPIO13, R4.Pin_1
  N15: R4.Pin_0, LED1.anode

custom parts:
  ESP32S-HiLetgo: HiLetgo ESP-WROOM-32 ESP32 ESP-32S Development Board 2.4GHz Dual-Mode WiFi + Bluetooth Dual Cores Microcontroller The ESP32 integrated with Antenna switches, RF Balun, power amplifiers, low-noise amplifiers, filters, and management modules, and the entire solution occupies the least area of PCB. 2.4 GHz Wi-Fi plus Bluetooth dual-mode chip, with TSMC Ultra-low power consumption 40nm technology,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
